// Logisim project labpr12.circ as structural Verilog: 1 circuit, main circuit main
module main (
  input  in_1,
  output out_2,
  output out_3,
  output out_4,
  output out_5,
  output out_6,
  output out_7,
  output out_8,
  output out_9
);

  wire and_1_out, clock_1_out;

  Clock clock_1 (.out(clock_1_out));
  not not_1 (out_6, out_2);
  J_K_Flip_Flop j_k_ff_1 (.J(in_1), .clk(clock_1_out), .K(in_1), .Q(out_5), .preset(and_1_out));  // open: Qn, en, reset
  not not_2 (out_7, out_3);
  and and_1 (and_1_out, out_7, out_6);
  J_K_Flip_Flop j_k_ff_2 (.J(in_1), .clk(out_5), .K(in_1), .Q(out_4), .preset(and_1_out));  // open: Qn, en, reset
  not not_3 (out_8, out_4);
  J_K_Flip_Flop j_k_ff_3 (.J(in_1), .clk(out_4), .K(in_1), .Q(out_3), .preset(and_1_out));  // open: Qn, en, reset
  not not_4 (out_9, out_5);
  J_K_Flip_Flop j_k_ff_4 (.J(in_1), .clk(out_3), .K(in_1), .Q(out_2), .preset(and_1_out));  // open: Qn, en, reset
endmodule
